// Logisim project TinyCPU.circ as structural Verilog: 17 circuits, main circuit TinyCPUMain
module TinyCPUMain (
  input  CLK,
  input  RESET
);

  wire DATAPATH_INSTANCE_acc_valid_out, DECODE_SIGNALS_accc_write_request, EFFECTIVE_OFFSET_MODE,
       EFFECTIVE_REGISTER_MODE, FETCH_DECODE_CONTROLS_add_address,
       FETCH_DECODE_CONTROLS_add_address_register, FETCH_DECODE_CONTROLS_add_address_register_plus_offset,
       FETCH_DECODE_CONTROLS_add_const, FETCH_DECODE_CONTROLS_and_address_register,
       FETCH_DECODE_CONTROLS_and_address_register_plus_offset, FETCH_DECODE_CONTROLS_clear_error,
       FETCH_DECODE_CONTROLS_div_address_register, FETCH_DECODE_CONTROLS_div_address_register_plus_offset,
       FETCH_DECODE_CONTROLS_load_address_register, FETCH_DECODE_CONTROLS_load_address_register_plus_offset,
       FETCH_DECODE_CONTROLS_mul_address_register, FETCH_DECODE_CONTROLS_mul_address_register_plus_offset,
       FETCH_DECODE_CONTROLS_not, FETCH_DECODE_CONTROLS_or_address_register,
       FETCH_DECODE_CONTROLS_or_address_register_plus_offset, FETCH_DECODE_CONTROLS_set_addr,
       FETCH_DECODE_CONTROLS_set_div0, FETCH_DECODE_CONTROLS_set_ill, FETCH_DECODE_CONTROLS_set_input,
       FETCH_DECODE_CONTROLS_set_inv, FETCH_DECODE_CONTROLS_set_ovf,
       FETCH_DECODE_CONTROLS_store_address_register,
       FETCH_DECODE_CONTROLS_store_address_register_plus_offset, FETCH_DECODE_CONTROLS_sub_address,
       FETCH_DECODE_CONTROLS_sub_address_register, FETCH_DECODE_CONTROLS_sub_address_register_plus_offset,
       FETCH_DECODE_CONTROLS_sub_const, MEMORY_INSTANCE_memory_valid, OPERATIONS_INSTANCE_result_is_valid;
  wire [15:0] ADDRESS_PATH_address, ADDRESS_PATH_address_plus_offset, DATAPATH_INSTANCE_acc_out,
       EFFECTIVE_ADDRESS_FBOX_effective_memory_address,
       EFFECTIVE_ADDRESS_FBOX_effective_register_selected_out, MEMORY_INSTANCE_memory_data,
       OPERATIONS_INSTANCE_result_value;
  wire [21:0] FETCH_DECODE_opcode;

  FetchDecode FETCH_DECODE (
    .CLK(CLK), .RESET(RESET), .OPCODE(FETCH_DECODE_opcode));  // open: DEC_JUMP_NOT_ZERO, NOT_ZERO, DEC_HALT_ERROR, PROGRAM_LIMIT, JUMP_NOT_ZERO, HALT_ERROR, PC_OUT
  Memory MEMORY_INSTANCE (
    .ADDRESS(EFFECTIVE_ADDRESS_FBOX_effective_memory_address), .CLK(CLK),
    .MEMORY_VALID(MEMORY_INSTANCE_memory_valid), .MEMORY_DATA(MEMORY_INSTANCE_memory_data));  // open: WRITE_ENABLE, VALID_IN, DATA_IN
  DecodeSignals DECODE_SIGNALS (
    .Opcode(FETCH_DECODE_opcode[21:16]), .ACC_MEMORY_REQUESST(MEMORY_INSTANCE_memory_valid),
    .ACCC_WRITE_REQUEST(DECODE_SIGNALS_accc_write_request));
  FetchDecodeControls FETCH_DECODE_CONTROLS (
    .OPCODE(FETCH_DECODE_opcode[21:16]), .LOAD_ADDRESS_REGISTER(FETCH_DECODE_CONTROLS_load_address_register),
    .LOAD_ADDRESS_REGISTER_PLUS_OFFSET(FETCH_DECODE_CONTROLS_load_address_register_plus_offset),
    .ADD_CONST(FETCH_DECODE_CONTROLS_add_const), .ADD_ADDRESS(FETCH_DECODE_CONTROLS_add_address),
    .ADD_ADDRESS_REGISTER(FETCH_DECODE_CONTROLS_add_address_register),
    .ADD_ADDRESS_REGISTER_PLUS_OFFSET(FETCH_DECODE_CONTROLS_add_address_register_plus_offset),
    .SUB_CONST(FETCH_DECODE_CONTROLS_sub_const), .SUB_ADDRESS(FETCH_DECODE_CONTROLS_sub_address),
    .SUB_ADDRESS_REGISTER(FETCH_DECODE_CONTROLS_sub_address_register),
    .SUB_ADDRESS_REGISTER_PLUS_OFFSET(FETCH_DECODE_CONTROLS_sub_address_register_plus_offset),
    .MUL_ADDRESS_REGISTER(FETCH_DECODE_CONTROLS_mul_address_register),
    .MUL_ADDRESS_REGISTER_PLUS_OFFSET(FETCH_DECODE_CONTROLS_mul_address_register_plus_offset),
    .DIV_ADDRESS_REGISTER(FETCH_DECODE_CONTROLS_div_address_register),
    .DIV_ADDRESS_REGISTER_PLUS_OFFSET(FETCH_DECODE_CONTROLS_div_address_register_plus_offset),
    .AND_ADDRESS_REGISTER(FETCH_DECODE_CONTROLS_and_address_register),
    .AND_ADDRESS_REGISTER_PLUS_OFFSET(FETCH_DECODE_CONTROLS_and_address_register_plus_offset),
    .OR_ADDRESS_REGISTER(FETCH_DECODE_CONTROLS_or_address_register),
    .OR_ADDRESS_REGISTER_PLUS_OFFSET(FETCH_DECODE_CONTROLS_or_address_register_plus_offset),
    .STORE_ADDRESS_REGISTER(FETCH_DECODE_CONTROLS_store_address_register),
    .STORE_ADDRESS_REGISTER_PLUS_OFFSET(FETCH_DECODE_CONTROLS_store_address_register_plus_offset),
    .NOT(FETCH_DECODE_CONTROLS_not), .CLEAR_ERROR(FETCH_DECODE_CONTROLS_clear_error),
    .SET_OVF(FETCH_DECODE_CONTROLS_set_ovf), .SET_DIV0(FETCH_DECODE_CONTROLS_set_div0),
    .SET_ADDR(FETCH_DECODE_CONTROLS_set_addr), .SET_INV(FETCH_DECODE_CONTROLS_set_inv),
    .SET_ILL(FETCH_DECODE_CONTROLS_set_ill), .SET_INPUT(FETCH_DECODE_CONTROLS_set_input));  // open: LOAD_CONST, LOAD_ADDRESS, MUL_CONST, MUL_ADDRESS, DIV_CONST, DIV_ADDRESS, AND_CONST, AND_ADDRESS, OR_CONST, OR_ADDRESS, STORE_ADDRESS, LOAD_ADDRESS_REGISTER_CONST, LOAD_ADDRESS_REGISTER_ADDRESS, JUMP_ADDRESS, JUMP_ZERO, JUMP_NEGATIVE, JUMP_ERROR, JUMP_NOT_ERROR, INPUT, PRINT, PRINT_ADDRESS, HALT, HALT_ERROR
  AddressPath ADDRESS_PATH (
    .AR_LOAD(DECODE_SIGNALS_accc_write_request), .ADDRESS(ADDRESS_PATH_address),
    .ADDRESS_PLUS_OFFSET(ADDRESS_PATH_address_plus_offset));  // open: ADDRESS_IN, OFFSET, VALID_IN, CLK, OFFSET_CARRY, ADDRESS_VALID
  Datapath DATAPATH_INSTANCE (
    .DATA_IN(OPERATIONS_INSTANCE_result_value), .VALID_IN(OPERATIONS_INSTANCE_result_is_valid), .CLK(CLK),
    .ACC_OUT(DATAPATH_INSTANCE_acc_out), .ACC_VALID_OUT(DATAPATH_INSTANCE_acc_valid_out));  // open: ACC_LOAD, ZERO, NEGATIVE
  ErrorFlags ERROR_FLAGS (
    .CLEAR_ERROR(FETCH_DECODE_CONTROLS_clear_error), .CLK(CLK), .SET_OVF(FETCH_DECODE_CONTROLS_set_ovf),
    .SET_DIV0(FETCH_DECODE_CONTROLS_set_div0), .SET_ADDR(FETCH_DECODE_CONTROLS_set_addr),
    .SET_INV(FETCH_DECODE_CONTROLS_set_inv), .SET_ILL(FETCH_DECODE_CONTROLS_set_ill),
    .SET_INPUT(FETCH_DECODE_CONTROLS_set_input));  // open: OVF_OUT, DIV0_OUT, ADDR_OUT, INV_OUT, ILL_OUT, INPUT_OUT
  Operations OPERATIONS_INSTANCE (
    .ADD_CONST(FETCH_DECODE_CONTROLS_add_const), .ADD_ADDRESS(FETCH_DECODE_CONTROLS_add_address),
    .ADD_ADDRESS_REGISTER(FETCH_DECODE_CONTROLS_add_address_register),
    .ADD_ADDRESS_REGISTER_PLUS_OFFSET(FETCH_DECODE_CONTROLS_add_address_register_plus_offset),
    .ACC_VALUE(DATAPATH_INSTANCE_acc_out), .MEMORY_VALUE(MEMORY_INSTANCE_memory_data),
    .IMMEDIATE_VALUE(FETCH_DECODE_opcode[15:0]), .MEMORY_VALID(MEMORY_INSTANCE_memory_valid),
    .ACC_VALID(DATAPATH_INSTANCE_acc_valid_out), .SUB_CONST(FETCH_DECODE_CONTROLS_sub_const),
    .SUB_ADDRESS(FETCH_DECODE_CONTROLS_sub_address),
    .SUB_ADDRESS_REGISTER(FETCH_DECODE_CONTROLS_sub_address_register),
    .SUB_ADDRESS_REGISTER_PLUS_OFFSET(FETCH_DECODE_CONTROLS_sub_address_register_plus_offset),
    .NOT_IS_ACTIVE(FETCH_DECODE_CONTROLS_not), .RESULT_VALUE(OPERATIONS_INSTANCE_result_value),
    .RESULT_IS_VALID(OPERATIONS_INSTANCE_result_is_valid));  // open: OVERFLOW
  EffectiveAddress EFFECTIVE_ADDRESS_FBOX (
    .EFFECTIVE_LOAD_REGISTER(FETCH_DECODE_CONTROLS_load_address_register),
    .EFFECTIVE_ADD_REGISTER(FETCH_DECODE_CONTROLS_add_address_register),
    .EFFECTIVE_SUB_REGISTER(FETCH_DECODE_CONTROLS_sub_address_register),
    .EFFECTIVE_MUL_REGISTER(FETCH_DECODE_CONTROLS_mul_address_register),
    .EFFECTIVE_STORE_REGISTER(FETCH_DECODE_CONTROLS_store_address_register),
    .EFFECTIVE_DIV_REGISTER(FETCH_DECODE_CONTROLS_div_address_register),
    .EFFECTIVE_AND_REGISTER(FETCH_DECODE_CONTROLS_and_address_register),
    .EFFECTIVE_OR_REGISTER(FETCH_DECODE_CONTROLS_or_address_register),
    .EFFECTIVE_LOAD_OFFSET(FETCH_DECODE_CONTROLS_load_address_register_plus_offset),
    .EFFECTIVE_ADD_OFFSET(FETCH_DECODE_CONTROLS_add_address_register_plus_offset),
    .EFFECTIVE_MUL_OFFSET(FETCH_DECODE_CONTROLS_mul_address_register_plus_offset),
    .EFFECTIVE_STORE_OFFSET(FETCH_DECODE_CONTROLS_store_address_register_plus_offset),
    .EFFECTIVE_DIV_OFFSET(FETCH_DECODE_CONTROLS_div_address_register_plus_offset),
    .EFFECTIVE_AND_OFFSET(FETCH_DECODE_CONTROLS_and_address_register_plus_offset),
    .EFFECTIVE_OR_OFFSET(FETCH_DECODE_CONTROLS_or_address_register_plus_offset),
    .EFFECTIVE_SUB_OFFSET(FETCH_DECODE_CONTROLS_sub_address_register_plus_offset),
    .EFFECTIVE_REGISTER_SELECTED(EFFECTIVE_ADDRESS_FBOX_effective_register_selected_out),
    .EFFECTIVE_OFFSET_ADDRESS(ADDRESS_PATH_address_plus_offset),
    .EFFECTIVE_DIRECT_ADDRESS(FETCH_DECODE_opcode[15:0]), .EFFECTIVE_REGISTER_ADDRESS(ADDRESS_PATH_address),
    .EFFECTIVE_MEMORY_ADDRESS(EFFECTIVE_ADDRESS_FBOX_effective_memory_address),
    .EFFECTIVE_REGISTER_SELECTED_OUT(EFFECTIVE_ADDRESS_FBOX_effective_register_selected_out),
    .EFFECTIVE_OFFSET_MODE(EFFECTIVE_OFFSET_MODE), .EFFECTIVE_REGISTER_MODE(EFFECTIVE_REGISTER_MODE));
endmodule

module EffectiveAddress (
  input  EFFECTIVE_LOAD_REGISTER,
  input  EFFECTIVE_ADD_REGISTER,
  input  EFFECTIVE_SUB_REGISTER,
  input  EFFECTIVE_MUL_REGISTER,
  input  EFFECTIVE_STORE_REGISTER,
  input  EFFECTIVE_DIV_REGISTER,
  input  EFFECTIVE_AND_REGISTER,
  input  EFFECTIVE_OR_REGISTER,
  input  EFFECTIVE_LOAD_OFFSET,
  input  EFFECTIVE_ADD_OFFSET,
  input  EFFECTIVE_MUL_OFFSET,
  input  EFFECTIVE_STORE_OFFSET,
  input  EFFECTIVE_DIV_OFFSET,
  input  EFFECTIVE_AND_OFFSET,
  input  EFFECTIVE_OR_OFFSET,
  input  EFFECTIVE_SUB_OFFSET,
  input  [15:0] EFFECTIVE_REGISTER_SELECTED,
  input  [15:0] EFFECTIVE_OFFSET_ADDRESS,
  input  [15:0] EFFECTIVE_DIRECT_ADDRESS,
  input  [15:0] EFFECTIVE_REGISTER_ADDRESS,
  output [15:0] EFFECTIVE_MEMORY_ADDRESS,
  output [15:0] EFFECTIVE_REGISTER_SELECTED_OUT,
  output EFFECTIVE_OFFSET_MODE,
  output EFFECTIVE_REGISTER_MODE
);

  or MEMORY_ADDRESS_REGISTER_SELECT (EFFECTIVE_REGISTER_MODE, EFFECTIVE_LOAD_REGISTER, EFFECTIVE_ADD_REGISTER, EFFECTIVE_SUB_REGISTER, EFFECTIVE_MUL_REGISTER, EFFECTIVE_STORE_REGISTER, EFFECTIVE_DIV_REGISTER, EFFECTIVE_AND_REGISTER, EFFECTIVE_OR_REGISTER);
  or MEMORY_ADDRESS_OFFSET_SELECT (EFFECTIVE_OFFSET_MODE, EFFECTIVE_LOAD_OFFSET, EFFECTIVE_ADD_OFFSET, EFFECTIVE_MUL_OFFSET, EFFECTIVE_STORE_OFFSET, EFFECTIVE_DIV_OFFSET, EFFECTIVE_AND_OFFSET, EFFECTIVE_OR_OFFSET, EFFECTIVE_SUB_OFFSET);
  Multiplexer #(.width(16)) multiplexer_1 (
    .in0(EFFECTIVE_OFFSET_ADDRESS), .in1(EFFECTIVE_REGISTER_SELECTED), .out(EFFECTIVE_MEMORY_ADDRESS),
    .sel(EFFECTIVE_OFFSET_MODE));
  Multiplexer #(.width(16)) multiplexer_2 (
    .in0(EFFECTIVE_DIRECT_ADDRESS), .in1(EFFECTIVE_REGISTER_ADDRESS), .out(EFFECTIVE_REGISTER_SELECTED_OUT),
    .sel(EFFECTIVE_REGISTER_MODE));

  // Other names for the same wires on the sheet: OFFSET_MODE_INTERNAL = EFFECTIVE_OFFSET_MODE;
  //   REGISTER_MODE_INTERNAL = EFFECTIVE_REGISTER_MODE
endmodule

module Datapath (
  input  [15:0] DATA_IN,
  input  ACC_LOAD,
  input  VALID_IN,
  input  CLK,
  output [15:0] ACC_OUT,
  output ZERO,
  output NEGATIVE,
  output ACC_VALID_OUT
);

  Register #(.width(16)) ACC (.D(DATA_IN), .en(ACC_LOAD), .clk(CLK), .Q(ACC_OUT));  // open: clr
  Register #(.width(1)) ACC_VALID (.D(VALID_IN), .en(CLK), .clk(ACC_LOAD), .Q(ACC_VALID_OUT));  // open: clr
  Comparator #(.width(16)) comparator_1 (.a(ACC_OUT), .b({16{1'b0}}), .eq(ZERO), .lt(NEGATIVE));  // open: gt

  // Notes on the sheet:
  //   Clocked 16-bit accumulator; signed comparator derives ZERO and NEGATIVE
endmodule

module AddressPath (
  input  [15:0] ADDRESS_IN,
  input  AR_LOAD,
  input  [15:0] OFFSET,
  input  VALID_IN,
  input  CLK,
  output [15:0] ADDRESS,
  output [15:0] ADDRESS_PLUS_OFFSET,
  output OFFSET_CARRY,
  output ADDRESS_VALID
);

  Register #(.width(16)) AR (.D(ADDRESS_IN), .en(AR_LOAD), .clk(CLK), .Q(ADDRESS));  // open: clr
  Register #(.width(1)) AR_VALID (.D(VALID_IN), .en(AR_LOAD), .clk(CLK), .Q(ADDRESS_VALID));  // open: clr
  Adder #(.width(16)) adder_1 (.a(ADDRESS), .b(OFFSET), .out(ADDRESS_PLUS_OFFSET), .cout(OFFSET_CARRY));  // open: cin

  // Notes on the sheet:
  //   Clocked 12-bit address register with combinational offset addition
endmodule

module Memory (
  input  [15:0] ADDRESS,
  input  WRITE_ENABLE,
  input  CLK,
  input  VALID_IN,
  input  [15:0] DATA_IN,
  output MEMORY_VALID,
  output [15:0] MEMORY_DATA
);

  RAM #(.addrWidth(12), .dataWidth(1)) VALID_RAM (
    .addr(ADDRESS[11:0]), .we(WRITE_ENABLE), .oe(1'b1), .clk(CLK), .din(VALID_IN), .dout(MEMORY_VALID));
  RAM #(.addrWidth(12), .dataWidth(16)) DATA_RAM (
    .addr(ADDRESS[11:0]), .we(WRITE_ENABLE), .oe(1'b1), .clk(CLK), .din(DATA_IN), .dout(MEMORY_DATA));

  // Notes on the sheet:
  //   4096-word value/valid memory with shared address, write-enable, and clock
endmodule

module ErrorFlags (
  input  CLEAR_ERROR,
  input  CLK,
  input  SET_OVF,
  input  SET_DIV0,
  input  SET_ADDR,
  input  SET_INV,
  input  SET_ILL,
  input  SET_INPUT,
  output OVF_OUT,
  output DIV0_OUT,
  output ADDR_OUT,
  output INV_OUT,
  output ILL_OUT,
  output INPUT_OUT
);

  wire HOLD_ADDR_out, HOLD_DIV0_out, HOLD_ILL_out, HOLD_INPUT_out, HOLD_INV_out, HOLD_OVF_out, NEXT_ADDR_out,
       NEXT_DIV0_out, NEXT_ILL_out, NEXT_INPUT_out, NEXT_INV_out, NEXT_OVF_out, NOT_CLEAR_ERROR_out;

  not NOT_CLEAR_ERROR (NOT_CLEAR_ERROR_out, CLEAR_ERROR);
  and HOLD_OVF (HOLD_OVF_out, OVF_OUT, NOT_CLEAR_ERROR_out);
  and HOLD_DIV0 (HOLD_DIV0_out, DIV0_OUT, NOT_CLEAR_ERROR_out);
  and HOLD_ADDR (HOLD_ADDR_out, ADDR_OUT, NOT_CLEAR_ERROR_out);
  and HOLD_INV (HOLD_INV_out, INV_OUT, NOT_CLEAR_ERROR_out);
  and HOLD_ILL (HOLD_ILL_out, ILL_OUT, NOT_CLEAR_ERROR_out);
  and HOLD_INPUT (HOLD_INPUT_out, INPUT_OUT, NOT_CLEAR_ERROR_out);
  or NEXT_OVF (NEXT_OVF_out, SET_OVF, HOLD_OVF_out);
  or NEXT_DIV0 (NEXT_DIV0_out, SET_DIV0, HOLD_DIV0_out);
  or NEXT_ADDR (NEXT_ADDR_out, SET_ADDR, HOLD_ADDR_out);
  or NEXT_INV (NEXT_INV_out, SET_INV, HOLD_INV_out);
  or NEXT_ILL (NEXT_ILL_out, SET_ILL, HOLD_ILL_out);
  or NEXT_INPUT (NEXT_INPUT_out, SET_INPUT, HOLD_INPUT_out);
  Register #(.width(1)) OVF (.D(NEXT_OVF_out), .en(1'b1), .clk(CLK), .Q(OVF_OUT));  // open: clr
  Register #(.width(1)) DIV0 (.D(NEXT_DIV0_out), .en(1'b1), .clk(CLK), .Q(DIV0_OUT));  // open: clr
  Register #(.width(1)) ADDR (.D(NEXT_ADDR_out), .en(1'b1), .clk(CLK), .Q(ADDR_OUT));  // open: clr
  Register #(.width(1)) INV (.D(NEXT_INV_out), .en(1'b1), .clk(CLK), .Q(INV_OUT));  // open: clr
  Register #(.width(1)) ILL (.D(NEXT_ILL_out), .en(1'b1), .clk(CLK), .Q(ILL_OUT));  // open: clr
  Register #(.width(1)) INPUT (.D(NEXT_INPUT_out), .en(1'b1), .clk(CLK), .Q(INPUT_OUT));  // open: clr

  // Notes on the sheet:
  //   Set-dominant sticky flags: SET OR (current AND NOT CLEAR_ERROR)
endmodule

module FetchDecode (
  input  DEC_JUMP_NOT_ZERO,
  input  NOT_ZERO,
  input  CLK,
  input  RESET,
  input  DEC_HALT_ERROR,
  input  [15:0] PROGRAM_LIMIT,
  output JUMP_NOT_ZERO,
  output HALT_ERROR,
  output [11:0] PC_OUT,
  output [21:0] OPCODE
);

  wire comparator_1_gt;
  wire [15:0] adder_1_out;
  wire [15:12] PC_q;

  Register #(.width(16)) PC (.D(adder_1_out), .en(1'b1), .clk(CLK), .Q({PC_q, PC_OUT}), .clr(RESET));
  Comparator #(.width(16)) comparator_1 (.a(PROGRAM_LIMIT), .b({PC_q, PC_OUT}), .gt(comparator_1_gt));  // open: eq, lt
  Adder #(.width(16)) adder_1 (.a({PC_q, PC_OUT}), .b({16{1'b1}}), .out(adder_1_out));  // open: cin, cout
  ROM #(.addrWidth(12), .dataWidth(22)) INSTRUCTION_ROM (.addr(PC_OUT), .data(OPCODE));
  and JNZ_TAKEN (JUMP_NOT_ZERO, DEC_JUMP_NOT_ZERO, NOT_ZERO);
  or ERROR_HALT (HALT_ERROR, comparator_1_gt, DEC_HALT_ERROR);

  // Notes on the sheet:
  //   PROGRAM_LIMIT: initial=0xfff
  //   AP 7 machine format v1: stable six-bit opcode allocation and encoder-generated ROM
  //   contents of INSTRUCTION_ROM (hex, n*v repeats v):
  //   ffff 1c0065 3 1c0064 2a0000 50065 1c0064 240004 2c0000
endmodule

module FetchDecodeControls (
  input  [5:0] OPCODE,
  output LOAD_CONST,
  output LOAD_ADDRESS,
  output LOAD_ADDRESS_REGISTER,
  output LOAD_ADDRESS_REGISTER_PLUS_OFFSET,
  output ADD_CONST,
  output ADD_ADDRESS,
  output ADD_ADDRESS_REGISTER,
  output ADD_ADDRESS_REGISTER_PLUS_OFFSET,
  output SUB_CONST,
  output SUB_ADDRESS,
  output SUB_ADDRESS_REGISTER,
  output SUB_ADDRESS_REGISTER_PLUS_OFFSET,
  output MUL_CONST,
  output MUL_ADDRESS,
  output MUL_ADDRESS_REGISTER,
  output MUL_ADDRESS_REGISTER_PLUS_OFFSET,
  output DIV_CONST,
  output DIV_ADDRESS,
  output DIV_ADDRESS_REGISTER,
  output DIV_ADDRESS_REGISTER_PLUS_OFFSET,
  output AND_CONST,
  output AND_ADDRESS,
  output AND_ADDRESS_REGISTER,
  output AND_ADDRESS_REGISTER_PLUS_OFFSET,
  output OR_CONST,
  output OR_ADDRESS,
  output OR_ADDRESS_REGISTER,
  output OR_ADDRESS_REGISTER_PLUS_OFFSET,
  output STORE_ADDRESS,
  output STORE_ADDRESS_REGISTER,
  output STORE_ADDRESS_REGISTER_PLUS_OFFSET,
  output LOAD_ADDRESS_REGISTER_CONST,
  output LOAD_ADDRESS_REGISTER_ADDRESS,
  output NOT,
  output JUMP_ADDRESS,
  output JUMP_ZERO,
  output JUMP_NEGATIVE,
  output JUMP_ERROR,
  output JUMP_NOT_ERROR,
  output CLEAR_ERROR,
  output INPUT,
  output PRINT,
  output PRINT_ADDRESS,
  output HALT,
  output HALT_ERROR,
  output SET_OVF,
  output SET_DIV0,
  output SET_ADDR,
  output SET_INV,
  output SET_ILL,
  output SET_INPUT
);

  Decoder #(.select(6)) decoder_1 (
    .out0(LOAD_CONST), .out1(LOAD_ADDRESS), .out2(LOAD_ADDRESS_REGISTER),
    .out3(LOAD_ADDRESS_REGISTER_PLUS_OFFSET), .out4(ADD_CONST), .out5(ADD_ADDRESS),
    .out6(ADD_ADDRESS_REGISTER), .out7(ADD_ADDRESS_REGISTER_PLUS_OFFSET), .out8(SUB_CONST),
    .out9(SUB_ADDRESS), .out10(SUB_ADDRESS_REGISTER), .out11(SUB_ADDRESS_REGISTER_PLUS_OFFSET),
    .out12(MUL_CONST), .out13(MUL_ADDRESS), .out14(MUL_ADDRESS_REGISTER),
    .out15(MUL_ADDRESS_REGISTER_PLUS_OFFSET), .out16(DIV_CONST), .out17(DIV_ADDRESS),
    .out18(DIV_ADDRESS_REGISTER), .out19(DIV_ADDRESS_REGISTER_PLUS_OFFSET), .out20(AND_CONST),
    .out21(AND_ADDRESS), .out22(AND_ADDRESS_REGISTER), .out23(AND_ADDRESS_REGISTER_PLUS_OFFSET),
    .out24(OR_CONST), .out25(OR_ADDRESS), .out26(OR_ADDRESS_REGISTER),
    .out27(OR_ADDRESS_REGISTER_PLUS_OFFSET), .out28(STORE_ADDRESS), .out29(STORE_ADDRESS_REGISTER),
    .out30(STORE_ADDRESS_REGISTER_PLUS_OFFSET), .out31(LOAD_ADDRESS_REGISTER_CONST),
    .out32(LOAD_ADDRESS_REGISTER_ADDRESS), .out33(NOT), .out34(JUMP_ADDRESS), .out35(JUMP_ZERO),
    .out36(JUMP_NEGATIVE), .out37(JUMP_ERROR), .out38(JUMP_NOT_ERROR), .out39(CLEAR_ERROR), .out40(INPUT),
    .out41(PRINT), .out42(PRINT_ADDRESS), .out43(HALT), .out44(HALT_ERROR), .out45(SET_OVF),
    .out46(SET_DIV0), .out47(SET_ADDR), .out48(SET_INV), .out49(SET_ILL), .out50(SET_INPUT), .sel(OPCODE));  // open: out51, out52, out53, out54, out55, out56, out57, out58, out59, out60, out61, out62, out63, en
endmodule

module IntegrationClock (
  input  CLK,
  output FETCH_CLK,
  output DATAPATH_CLK,
  output ADDRESS_CLK,
  output MEMORY_CLK,
  output ERROR_FLAGS_CLK
);


  assign ADDRESS_CLK = CLK;
  assign DATAPATH_CLK = CLK;
  assign ERROR_FLAGS_CLK = CLK;
  assign FETCH_CLK = CLK;
  assign MEMORY_CLK = CLK;
endmodule

module IntegrationReset (
  input  RESET,
  output FETCH_RESET
);


  assign FETCH_RESET = RESET;
endmodule

module Operations (
  input  ADD_CONST,
  input  ADD_ADDRESS,
  input  ADD_ADDRESS_REGISTER,
  input  ADD_ADDRESS_REGISTER_PLUS_OFFSET,
  input  [15:0] ACC_VALUE,
  input  [15:0] MEMORY_VALUE,
  input  [15:0] IMMEDIATE_VALUE,
  input  MEMORY_VALID,
  input  ACC_VALID,
  input  SUB_CONST,
  input  SUB_ADDRESS,
  input  SUB_ADDRESS_REGISTER,
  input  SUB_ADDRESS_REGISTER_PLUS_OFFSET,
  input  NOT_IS_ACTIVE,
  output [15:0] RESULT_VALUE,
  output RESULT_IS_VALID,
  output OVERFLOW
);

  wire ADD_OPERATION_overflow, ADD_OPERATION_result_valid, NOT_OPERATION_result_valid,
       SUB_OPERATION_overflow, SUB_OPERATION_result_valid;
  wire [15:0] ADD_OPERATION_result, NOT_OPERATION_result, SUB_OPERATION_result;

  AddSubCircuit ADD_OPERATION (
    .ADD_CONST(ADD_CONST), .ADD_ADDRESS(ADD_ADDRESS), .ADD_ADDRESS_REGISTER(ADD_ADDRESS_REGISTER),
    .ADD_ADDRESS_REGISTER_PLUS_OFFSET(ADD_ADDRESS_REGISTER_PLUS_OFFSET), .ACC_VALUE(ACC_VALUE),
    .MEMORY_VALUE(MEMORY_VALUE), .IMMEDIATE_VALUE(IMMEDIATE_VALUE), .MEMORY_VALID(MEMORY_VALID),
    .ACC_VALID(ACC_VALID), .RESULT(ADD_OPERATION_result), .OVERFLOW(ADD_OPERATION_overflow),
    .RESULT_VALID(ADD_OPERATION_result_valid));
  SubSubCircuit SUB_OPERATION (
    .SUB_CONST(SUB_CONST), .SUB_ADDRESS_REGISTER_PLUS_OFFSET(SUB_ADDRESS),
    .SUB_ADDRESS(SUB_ADDRESS_REGISTER), .SUB_ADDRESS_REGISTER(SUB_ADDRESS_REGISTER_PLUS_OFFSET),
    .ACC_VALUE(ACC_VALUE), .MEMORY_VALUE(MEMORY_VALUE), .IMMEDIATE_VALUE(IMMEDIATE_VALUE),
    .MEMORY_VALID(MEMORY_VALID), .ACC_VALID(ACC_VALID), .RESULT(SUB_OPERATION_result),
    .OVERFLOW(SUB_OPERATION_overflow), .RESULT_VALID(SUB_OPERATION_result_valid));
  NotCircuit NOT_OPERATION (
    .ACC_VALUE(ACC_VALUE), .ACC_VALID(ACC_VALID), .NOT_IS_ACTIVE(NOT_IS_ACTIVE),
    .RESULT(NOT_OPERATION_result), .RESULT_VALID(NOT_OPERATION_result_valid));
  assign RESULT_VALUE = ADD_OPERATION_result | SUB_OPERATION_result | NOT_OPERATION_result;  // OR_Gate RESULT, 16 bits wide
  or RESULT_VALID (RESULT_IS_VALID, ADD_OPERATION_result_valid, SUB_OPERATION_result_valid, NOT_OPERATION_result_valid);
  or OVERFLOW_SET (OVERFLOW, ADD_OPERATION_overflow, SUB_OPERATION_overflow);
endmodule

module NotCircuit (
  input  [15:0] ACC_VALUE,
  input  ACC_VALID,
  input  NOT_IS_ACTIVE,
  output [15:0] RESULT,
  output RESULT_VALID
);

  wire [15:0] NOT_VALUE_out;

  assign NOT_VALUE_out = ~ACC_VALUE;  // NOT_Gate NOT_VALUE, 16 bits wide
  and ACTIVE_NOT_VALID (RESULT_VALID, ACC_VALID, NOT_IS_ACTIVE);
  Multiplexer #(.width(16)) multiplexer_1 (.in0({16{1'b0}}), .in1(NOT_VALUE_out), .out(RESULT), .sel(NOT_IS_ACTIVE));
endmodule

module DecodeSignals (
  input  [5:0] Opcode,
  output ACC_MEMORY_REQUESST,
  output ACCC_WRITE_REQUEST
);

  wire ACC_LOAD_REQUEST_out, CONTROL_DECODER_add_address, CONTROL_DECODER_add_address_register,
       CONTROL_DECODER_add_address_register_plus_offset, CONTROL_DECODER_add_const,
       CONTROL_DECODER_and_address, CONTROL_DECODER_and_address_register,
       CONTROL_DECODER_and_address_register_plus_offset, CONTROL_DECODER_and_const,
       CONTROL_DECODER_div_address, CONTROL_DECODER_div_address_register,
       CONTROL_DECODER_div_address_register_plus_offset, CONTROL_DECODER_div_const, CONTROL_DECODER_input,
       CONTROL_DECODER_load_address, CONTROL_DECODER_load_address_register,
       CONTROL_DECODER_load_address_register_const, CONTROL_DECODER_load_address_register_plus_offset,
       CONTROL_DECODER_load_const, CONTROL_DECODER_mul_address, CONTROL_DECODER_mul_address_register,
       CONTROL_DECODER_mul_address_register_plus_offset, CONTROL_DECODER_mul_const, CONTROL_DECODER_not,
       CONTROL_DECODER_or_address, CONTROL_DECODER_or_address_register,
       CONTROL_DECODER_or_address_register_plus_offset, CONTROL_DECODER_or_const,
       CONTROL_DECODER_store_address, CONTROL_DECODER_store_address_register,
       CONTROL_DECODER_store_address_register_plus_offset, CONTROL_DECODER_sub_address,
       CONTROL_DECODER_sub_address_register, CONTROL_DECODER_sub_address_register_plus_offset,
       CONTROL_DECODER_sub_const;

  FetchDecodeControls CONTROL_DECODER (
    .OPCODE(Opcode), .LOAD_CONST(CONTROL_DECODER_load_const), .LOAD_ADDRESS(CONTROL_DECODER_load_address),
    .LOAD_ADDRESS_REGISTER(CONTROL_DECODER_load_address_register),
    .LOAD_ADDRESS_REGISTER_PLUS_OFFSET(CONTROL_DECODER_load_address_register_plus_offset),
    .ADD_CONST(CONTROL_DECODER_add_const), .ADD_ADDRESS(CONTROL_DECODER_add_address),
    .ADD_ADDRESS_REGISTER(CONTROL_DECODER_add_address_register),
    .ADD_ADDRESS_REGISTER_PLUS_OFFSET(CONTROL_DECODER_add_address_register_plus_offset),
    .SUB_CONST(CONTROL_DECODER_sub_const), .SUB_ADDRESS(CONTROL_DECODER_sub_address),
    .SUB_ADDRESS_REGISTER(CONTROL_DECODER_sub_address_register),
    .SUB_ADDRESS_REGISTER_PLUS_OFFSET(CONTROL_DECODER_sub_address_register_plus_offset),
    .MUL_CONST(CONTROL_DECODER_mul_const), .MUL_ADDRESS(CONTROL_DECODER_mul_address),
    .MUL_ADDRESS_REGISTER(CONTROL_DECODER_mul_address_register),
    .MUL_ADDRESS_REGISTER_PLUS_OFFSET(CONTROL_DECODER_mul_address_register_plus_offset),
    .DIV_CONST(CONTROL_DECODER_div_const), .DIV_ADDRESS(CONTROL_DECODER_div_address),
    .DIV_ADDRESS_REGISTER(CONTROL_DECODER_div_address_register),
    .DIV_ADDRESS_REGISTER_PLUS_OFFSET(CONTROL_DECODER_div_address_register_plus_offset),
    .AND_CONST(CONTROL_DECODER_and_const), .AND_ADDRESS(CONTROL_DECODER_and_address),
    .AND_ADDRESS_REGISTER(CONTROL_DECODER_and_address_register),
    .AND_ADDRESS_REGISTER_PLUS_OFFSET(CONTROL_DECODER_and_address_register_plus_offset),
    .OR_CONST(CONTROL_DECODER_or_const), .OR_ADDRESS(CONTROL_DECODER_or_address),
    .OR_ADDRESS_REGISTER(CONTROL_DECODER_or_address_register),
    .OR_ADDRESS_REGISTER_PLUS_OFFSET(CONTROL_DECODER_or_address_register_plus_offset),
    .STORE_ADDRESS(CONTROL_DECODER_store_address),
    .STORE_ADDRESS_REGISTER(CONTROL_DECODER_store_address_register),
    .STORE_ADDRESS_REGISTER_PLUS_OFFSET(CONTROL_DECODER_store_address_register_plus_offset),
    .LOAD_ADDRESS_REGISTER_CONST(CONTROL_DECODER_load_address_register_const), .NOT(CONTROL_DECODER_not),
    .INPUT(CONTROL_DECODER_input));  // open: LOAD_ADDRESS_REGISTER_ADDRESS, JUMP_ADDRESS, JUMP_ZERO, JUMP_NEGATIVE, JUMP_ERROR, JUMP_NOT_ERROR, CLEAR_ERROR, PRINT, PRINT_ADDRESS, HALT, HALT_ERROR, SET_OVF, SET_DIV0, SET_ADDR, SET_INV, SET_ILL, SET_INPUT
  or ACC_LOAD_REQUEST (ACC_LOAD_REQUEST_out, CONTROL_DECODER_load_const, CONTROL_DECODER_load_address, CONTROL_DECODER_load_address_register, CONTROL_DECODER_load_address_register_plus_offset, CONTROL_DECODER_add_const, CONTROL_DECODER_add_address, CONTROL_DECODER_add_address_register, CONTROL_DECODER_add_address_register_plus_offset, CONTROL_DECODER_sub_const, CONTROL_DECODER_sub_address, CONTROL_DECODER_sub_address_register, CONTROL_DECODER_sub_address_register_plus_offset, CONTROL_DECODER_mul_const, CONTROL_DECODER_mul_address, CONTROL_DECODER_mul_address_register, CONTROL_DECODER_mul_address_register_plus_offset, CONTROL_DECODER_div_const, CONTROL_DECODER_div_address, CONTROL_DECODER_div_address_register, CONTROL_DECODER_div_address_register_plus_offset, CONTROL_DECODER_and_const, CONTROL_DECODER_and_address, CONTROL_DECODER_and_address_register, CONTROL_DECODER_and_address_register_plus_offset, CONTROL_DECODER_or_const, CONTROL_DECODER_or_address, CONTROL_DECODER_or_address_register, CONTROL_DECODER_or_address_register_plus_offset, CONTROL_DECODER_store_address, CONTROL_DECODER_store_address_register, CONTROL_DECODER_store_address_register_plus_offset, CONTROL_DECODER_load_address_register_const);
  or ACC_MEMORY_SELECT (ACC_MEMORY_REQUESST, CONTROL_DECODER_load_address, CONTROL_DECODER_load_address_register, CONTROL_DECODER_load_address_register_plus_offset);
  or ACC_WRITE_REQUEST (ACCC_WRITE_REQUEST, ACC_LOAD_REQUEST_out, CONTROL_DECODER_not, CONTROL_DECODER_input);
endmodule

module AddSubCircuit (
  input  ADD_CONST,
  input  ADD_ADDRESS,
  input  ADD_ADDRESS_REGISTER,
  input  ADD_ADDRESS_REGISTER_PLUS_OFFSET,
  input  [15:0] ACC_VALUE,
  input  [15:0] MEMORY_VALUE,
  input  [15:0] IMMEDIATE_VALUE,
  input  MEMORY_VALID,
  input  ACC_VALID,
  output [15:0] RESULT,
  output OVERFLOW,
  output RESULT_VALID
);

  wire ACC_ADD_MEMORY_SELECT_out, ACC_ADD_VALID_out, multiplexer_2_out;
  wire [15:0] multiplexer_1_out;

  Multiplexer #(.width(16)) multiplexer_1 (
    .in0(MEMORY_VALUE), .in1(IMMEDIATE_VALUE), .out(multiplexer_1_out), .sel(ADD_CONST));
  Multiplexer multiplexer_2 (.in0(MEMORY_VALID), .in1(1'b1), .out(multiplexer_2_out), .sel(ADD_CONST));
  or ACC_ADD_MEMORY_SELECT (ACC_ADD_MEMORY_SELECT_out, ADD_CONST, ADD_ADDRESS, ADD_ADDRESS_REGISTER, ADD_ADDRESS_REGISTER_PLUS_OFFSET);
  and ACC_ADD_VALID (ACC_ADD_VALID_out, multiplexer_2_out, ACC_VALID);
  AddArithmeticCircuit ADDARITHMETICCIRCUIT_1300_440 (
    .ADD_ACTIVATED(ACC_ADD_MEMORY_SELECT_out), .LEFT(ACC_VALUE), .RIGHT(multiplexer_1_out),
    .INPUT_VALID(ACC_ADD_VALID_out), .RESULT(RESULT), .OVERFLOW(OVERFLOW), .RESULT_VALID(RESULT_VALID));

  // Notes on the sheet:
  //   MEMORY_VALID →
  //   ADD_VALID →
  //   CONST_VALID →
endmodule

module SubSubCircuit (
  input  SUB_CONST,
  input  SUB_ADDRESS_REGISTER_PLUS_OFFSET,
  input  SUB_ADDRESS,
  input  SUB_ADDRESS_REGISTER,
  input  [15:0] ACC_VALUE,
  input  [15:0] MEMORY_VALUE,
  input  [15:0] IMMEDIATE_VALUE,
  input  MEMORY_VALID,
  input  ACC_VALID,
  output [15:0] RESULT,
  output OVERFLOW,
  output RESULT_VALID
);

  wire ACC_ADD_VALID_out, ACC_SUB_MEMORY_SELECT_out, multiplexer_2_out;
  wire [15:0] multiplexer_1_out;

  or ACC_SUB_MEMORY_SELECT (ACC_SUB_MEMORY_SELECT_out, SUB_CONST, SUB_ADDRESS_REGISTER_PLUS_OFFSET, SUB_ADDRESS, SUB_ADDRESS_REGISTER);
  Multiplexer #(.width(16)) multiplexer_1 (
    .in0(MEMORY_VALUE), .in1(IMMEDIATE_VALUE), .out(multiplexer_1_out), .sel(SUB_CONST));
  Multiplexer multiplexer_2 (.in0(MEMORY_VALID), .in1(1'b1), .out(multiplexer_2_out), .sel(SUB_CONST));
  and ACC_ADD_VALID (ACC_ADD_VALID_out, multiplexer_2_out, ACC_VALID);
  SubArithmeticCircuit SUBARITHMETICCIRCUIT_1300_440 (
    .SUB_ACTIVATED(ACC_SUB_MEMORY_SELECT_out), .LEFT(ACC_VALUE), .RIGHT(multiplexer_1_out),
    .INPUT_VALID(ACC_ADD_VALID_out), .RESULT(RESULT), .OVERFLOW(OVERFLOW), .RESULT_VALID(RESULT_VALID));

  // Notes on the sheet:
  //   MEMORY_VALID →
  //   ADD_VALID →
  //   CONST_VALID →
endmodule

module AddArithmeticCircuit (
  input  ADD_ACTIVATED,
  input  [15:0] LEFT,
  input  [15:0] RIGHT,
  input  INPUT_VALID,
  output [15:0] RESULT,
  output OVERFLOW,
  output RESULT_VALID
);

  wire NO_OVERFLOW_out, OPERAND_SIGN_DIFFERENT_out, OPERAND_SIGN_SAME_out, RESULT_SIGN_CHANGED_out;
  wire [14:0] multiplexer_2_out;
  wire [15:0] multiplexer_1_out;
  wire [15:15] multiplexer_2_out_2;

  Multiplexer #(.width(16)) multiplexer_1 (.in0({16{1'b0}}), .in1(LEFT), .out(multiplexer_1_out), .sel(ADD_ACTIVATED));
  Multiplexer #(.width(16)) multiplexer_2 (
    .in0({16{1'b0}}), .in1(RIGHT), .out({multiplexer_2_out_2[15], multiplexer_2_out}), .sel(ADD_ACTIVATED));
  Adder #(.width(16)) adder_1 (
    .a(multiplexer_1_out), .b({multiplexer_2_out_2[15], multiplexer_2_out}), .out(RESULT));  // open: cin, cout
  xor OPERAND_SIGN_DIFFERENT (OPERAND_SIGN_DIFFERENT_out, multiplexer_1_out[15], multiplexer_2_out_2[15]);
  not OPERAND_SIGN_SAME (OPERAND_SIGN_SAME_out, OPERAND_SIGN_DIFFERENT_out);
  xor RESULT_SIGN_CHANGED (RESULT_SIGN_CHANGED_out, RESULT[15], multiplexer_1_out[15]);
  not NO_OVERFLOW (NO_OVERFLOW_out, OPERAND_SIGN_SAME_out);
  and SIGN_OVERFLOW (OVERFLOW, RESULT_SIGN_CHANGED_out, OPERAND_SIGN_SAME_out);
  and RANGE_VALID (RESULT_VALID, NO_OVERFLOW_out, INPUT_VALID);

  // Notes on the sheet:
  //   signed ADD: overflow = NOT(left_sign XOR right_sign) AND (left_sign XOR result_sign)
endmodule

module SubArithmeticCircuit (
  input  SUB_ACTIVATED,
  input  [15:0] LEFT,
  input  [15:0] RIGHT,
  input  INPUT_VALID,
  output [15:0] RESULT,
  output OVERFLOW,
  output RESULT_VALID
);

  wire NO_OVERFLOW_out, OPERAND_SIGN_DIFFERENT_out, RESULT_SIGN_CHANGED_out;
  wire [14:0] multiplexer_2_out;
  wire [15:0] multiplexer_1_out;
  wire [15:15] multiplexer_2_out_2;

  Multiplexer #(.width(16)) multiplexer_1 (.in0({16{1'b0}}), .in1(LEFT), .out(multiplexer_1_out), .sel(SUB_ACTIVATED));
  Multiplexer #(.width(16)) multiplexer_2 (
    .in0({16{1'b0}}), .in1(RIGHT), .out({multiplexer_2_out_2[15], multiplexer_2_out}), .sel(SUB_ACTIVATED));
  Subtractor #(.width(16)) subtractor_1 (
    .a(multiplexer_1_out), .b({multiplexer_2_out_2[15], multiplexer_2_out}), .out(RESULT));  // open: bin, bout
  xor OPERAND_SIGN_DIFFERENT (OPERAND_SIGN_DIFFERENT_out, multiplexer_1_out[15], multiplexer_2_out_2[15]);
  xor RESULT_SIGN_CHANGED (RESULT_SIGN_CHANGED_out, RESULT[15], multiplexer_1_out[15]);
  not NO_OVERFLOW (NO_OVERFLOW_out, OPERAND_SIGN_DIFFERENT_out);
  and SIGN_OVERFLOW (OVERFLOW, RESULT_SIGN_CHANGED_out, OPERAND_SIGN_DIFFERENT_out);
  and RANGE_VALID (RESULT_VALID, NO_OVERFLOW_out, INPUT_VALID);

  // Notes on the sheet:
  //   signed SUB: overflow = (left_sign XOR right_sign) AND (left_sign XOR result_sign)
endmodule
