// Logisim project TinyCPU-AddSub.circ as structural Verilog: 1 circuit, main circuit AddSub
module AddSub (
  input  [31:0] OPERANDS,
  input  SUBTRACT,
  input  [1:0] VALID,
  output CARRY,
  output [15:0] RESULT,
  output RESULT_VALID
);

  wire BOTH_VALID_out;
  wire [15:0] ADD_VALUE_out, SUB_VALUE_out;

  Adder #(.width(16)) ADD_VALUE (
    .a(OPERANDS[15:0]), .b(OPERANDS[31:16]), .out(ADD_VALUE_out), .cin(1'b1), .cout(CARRY));
  Subtractor #(.width(16)) SUB_VALUE (.a(OPERANDS[15:0]), .b(OPERANDS[31:16]), .out(SUB_VALUE_out));  // open: bin, bout
  and BOTH_VALID (BOTH_VALID_out, VALID[0], VALID[1]);
  and ACTIVE_VALID (RESULT_VALID, SUBTRACT, BOTH_VALID_out);
  Multiplexer #(.width(16)) ADD_SUB_RESULT_SELECT (
    .in0(ADD_VALUE_out), .in1(SUB_VALUE_out), .out(RESULT), .sel(SUBTRACT));

  // Notes on the sheet:
  //   ADD / SUB — gebündelte Operanden- und Validitätsbusse
endmodule
