// Logisim project TinyCPU-AddValidCircuit.circ as structural Verilog: 1 circuit, main circuit AddValidCircuit
module AddValidCircuit (
  input  ADD_ADDRESS,
  input  ADD_ADDRESS_REGISTER,
  input  ADD_ADDRESS_REGISTER_PLUS_OFFSET,
  input  ADD_CONST,
  input  MEMORY_VALID,
  input  ACC_VALID,
  output ADD_VALID
);

  wire ACC_ADD_FAMILY_SELECT_out, ACC_ADD_MEMORY_SELECT_out, multiplexer_1_out;

  buf ACC_ADD_MEMORY_SELECT (ACC_ADD_MEMORY_SELECT_out, ADD_ADDRESS_REGISTER);  // OR_Gate
  or ACC_ADD_FAMILY_SELECT (ACC_ADD_FAMILY_SELECT_out, ACC_ADD_MEMORY_SELECT_out, ADD_CONST);
  Multiplexer multiplexer_1 (.in0(1'b1), .in1(MEMORY_VALID), .out(multiplexer_1_out));  // open: sel
  and ACC_ADD_VALID (ADD_VALID, multiplexer_1_out, ACC_VALID);

  // Notes on the sheet:
  //   ADD_ADDRESS/CONST_VALID →
  //   ADD_OPERAND_VALID →
  //   ADD_VALID →
endmodule
