// Logisim project TinyCPU-AddressRangeFBox.circ as structural Verilog: 1 circuit, main circuit AddressRangeFBox
module AddressRangeFBox (
  input  LOAD_ADDRESS,
  input  ADD_ADDRESS,
  input  SUB_ADDRESS,
  input  MUL_ADDRESS,
  input  DIV_ADDRESS,
  input  AND_ADDRESS,
  input  OR_ADDRESS,
  input  STORE_ADDRESS,
  input  EFFECTIVE_REGISTER_MODE,
  input  EFFECTIVE_OFFSET_MODE,
  input  ADDRESS_OUT_OF_RANGE,
  output ACTIVE_ADDRESS_OUT_OF_RANGE
);

  wire DIRECT_MEMORY_ADDRESS_ACTIVE_out, MEMORY_ADDRESS_ACTIVE_out;

  or DIRECT_MEMORY_ADDRESS_ACTIVE (DIRECT_MEMORY_ADDRESS_ACTIVE_out, MUL_ADDRESS, LOAD_ADDRESS, ADD_ADDRESS, SUB_ADDRESS, DIV_ADDRESS, AND_ADDRESS, OR_ADDRESS, STORE_ADDRESS);
  or MEMORY_ADDRESS_ACTIVE (MEMORY_ADDRESS_ACTIVE_out, EFFECTIVE_REGISTER_MODE, EFFECTIVE_OFFSET_MODE, DIRECT_MEMORY_ADDRESS_ACTIVE_out);
  and ACTIVE_ADDRESS_RANGE_GATE (ACTIVE_ADDRESS_OUT_OF_RANGE, ADDRESS_OUT_OF_RANGE, MEMORY_ADDRESS_ACTIVE_out);
endmodule
