// Logisim project TinyCPU-DivArithmeticCircuit.circ as structural Verilog: 1 circuit, main circuit DivArithmeticCircuit
module DivArithmeticCircuit (
  input  DIV_ACTIVATED,
  input  [15:0] LEFT,
  input  [15:0] RIGHT,
  input  INPUT_VALID,
  output [15:0] RESULT,
  output OVERFLOW,
  output RESULT_VALID,
  output DIVIDE_BY_ZERO
);

  wire NO_OVERFLOW_out, NONZERO_DIVISOR_out, OPERAND_SIGN_DIFFERENT_out, RESULT_SIGN_CHANGED_out;
  wire [14:0] multiplexer_2_out;
  wire [15:0] multiplexer_1_out;
  wire [15:15] multiplexer_2_out_2;

  Multiplexer #(.width(16)) multiplexer_1 (.in0({16{1'b0}}), .in1(LEFT), .out(multiplexer_1_out), .sel(DIV_ACTIVATED));
  Multiplexer #(.width(16)) multiplexer_2 (
    .in0({16{1'b0}}), .in1(RIGHT), .out({multiplexer_2_out_2[15], multiplexer_2_out}), .sel(DIV_ACTIVATED));
  Divider #(.width(16)) divider_1 (
    .a(multiplexer_1_out), .b({multiplexer_2_out_2[15], multiplexer_2_out}), .out(RESULT));  // open: upper, rem
  xor OPERAND_SIGN_DIFFERENT (OPERAND_SIGN_DIFFERENT_out, multiplexer_1_out[15], multiplexer_2_out_2[15]);
  xor RESULT_SIGN_CHANGED (RESULT_SIGN_CHANGED_out, RESULT[15], multiplexer_1_out[15]);
  Comparator #(.width(16)) DIVISOR_ZERO_CHECK (
    .a({multiplexer_2_out_2[15], multiplexer_2_out}), .b(16'h1), .eq(DIVIDE_BY_ZERO));  // open: gt, lt
  not NO_OVERFLOW (NO_OVERFLOW_out, OPERAND_SIGN_DIFFERENT_out);
  not NONZERO_DIVISOR (NONZERO_DIVISOR_out, DIVIDE_BY_ZERO);
  and SIGN_OVERFLOW (OVERFLOW, RESULT_SIGN_CHANGED_out, OPERAND_SIGN_DIFFERENT_out);
  and RANGE_VALID (RESULT_VALID, NO_OVERFLOW_out, NONZERO_DIVISOR_out, INPUT_VALID);

  // Notes on the sheet:
  //   signed DIV: overflow = (left_sign XOR right_sign) AND (left_sign XOR result_sign)
endmodule
