// Logisim project TinyCPU-EffectiveAddress.circ as structural Verilog: 1 circuit, main circuit EffectiveAddress
module EffectiveAddress (
  input  EFFECTIVE_LOAD_REGISTER,
  input  EFFECTIVE_ADD_REGISTER,
  input  EFFECTIVE_SUB_REGISTER,
  input  EFFECTIVE_MUL_REGISTER,
  input  EFFECTIVE_STORE_REGISTER,
  input  EFFECTIVE_DIV_REGISTER,
  input  EFFECTIVE_AND_REGISTER,
  input  EFFECTIVE_OR_REGISTER,
  input  EFFECTIVE_LOAD_OFFSET,
  input  EFFECTIVE_ADD_OFFSET,
  input  EFFECTIVE_MUL_OFFSET,
  input  EFFECTIVE_STORE_OFFSET,
  input  EFFECTIVE_DIV_OFFSET,
  input  EFFECTIVE_AND_OFFSET,
  input  EFFECTIVE_OR_OFFSET,
  input  EFFECTIVE_SUB_OFFSET,
  input  [15:0] EFFECTIVE_REGISTER_SELECTED,
  input  [15:0] EFFECTIVE_OFFSET_ADDRESS,
  input  [15:0] EFFECTIVE_DIRECT_ADDRESS,
  input  [15:0] EFFECTIVE_REGISTER_ADDRESS,
  output [15:0] EFFECTIVE_MEMORY_ADDRESS,
  output [15:0] EFFECTIVE_REGISTER_SELECTED_OUT,
  output EFFECTIVE_OFFSET_MODE,
  output EFFECTIVE_REGISTER_MODE
);

  or MEMORY_ADDRESS_REGISTER_SELECT (EFFECTIVE_REGISTER_MODE, EFFECTIVE_LOAD_REGISTER, EFFECTIVE_ADD_REGISTER, EFFECTIVE_SUB_REGISTER, EFFECTIVE_MUL_REGISTER, EFFECTIVE_STORE_REGISTER, EFFECTIVE_DIV_REGISTER, EFFECTIVE_AND_REGISTER, EFFECTIVE_OR_REGISTER);
  or MEMORY_ADDRESS_OFFSET_SELECT (EFFECTIVE_OFFSET_MODE, EFFECTIVE_LOAD_OFFSET, EFFECTIVE_ADD_OFFSET, EFFECTIVE_MUL_OFFSET, EFFECTIVE_STORE_OFFSET, EFFECTIVE_DIV_OFFSET, EFFECTIVE_AND_OFFSET, EFFECTIVE_OR_OFFSET, EFFECTIVE_SUB_OFFSET);
  Multiplexer #(.width(16)) MEMORY_OFFSET_ADDRESS_SELECT (
    .in0(EFFECTIVE_OFFSET_ADDRESS), .in1(EFFECTIVE_REGISTER_SELECTED), .out(EFFECTIVE_MEMORY_ADDRESS),
    .sel(EFFECTIVE_OFFSET_MODE));
  Multiplexer #(.width(16)) MEMORY_REGISTER_ADDRESS_SELECT (
    .in0(EFFECTIVE_DIRECT_ADDRESS), .in1(EFFECTIVE_REGISTER_ADDRESS), .out(EFFECTIVE_REGISTER_SELECTED_OUT),
    .sel(EFFECTIVE_REGISTER_MODE));

  // Other names for the same wires on the sheet: OFFSET_MODE_INTERNAL = EFFECTIVE_OFFSET_MODE;
  //   REGISTER_MODE_INTERNAL = EFFECTIVE_REGISTER_MODE
endmodule
