// Logisim project TinyCPU-FetchDecode.circ as structural Verilog: 1 circuit, main circuit FetchDecode
module FetchDecode (
  input  DEC_JUMP_NOT_ZERO,
  input  NOT_ZERO,
  input  CLK,
  input  RESET,
  input  [15:0] PROGRAM_LIMIT,
  input  DEC_HALT_ERROR,
  input  ZERO,
  input  NEGATIVE,
  input  ERROR,
  input  [15:0] OPERAND,
  input  [5:0] OPCODE,
  output LOAD_CONST,
  output LOAD_ADDRESS,
  output LOAD_ADDRESS_REGISTER,
  output LOAD_ADDRESS_REGISTER_PLUS_OFFSET,
  output ADD_CONST,
  output ADD_ADDRESS,
  output ADD_ADDRESS_REGISTER,
  output JUMP_NOT_ZERO,
  output ADD_ADDRESS_REGISTER_PLUS_OFFSET,
  output SUB_CONST,
  output SUB_ADDRESS,
  output SUB_ADDRESS_REGISTER,
  output HALT_ERROR,
  output SUB_ADDRESS_REGISTER_PLUS_OFFSET,
  output MUL_CONST,
  output MUL_ADDRESS,
  output MUL_ADDRESS_REGISTER,
  output MUL_ADDRESS_REGISTER_PLUS_OFFSET,
  output DIV_CONST,
  output [15:0] PC_OUT,
  output DIV_ADDRESS,
  output DIV_ADDRESS_REGISTER,
  output DIV_ADDRESS_REGISTER_PLUS_OFFSET,
  output AND_CONST,
  output AND_ADDRESS,
  output AND_ADDRESS_REGISTER,
  output AND_ADDRESS_REGISTER_PLUS_OFFSET,
  output [21:0] OPCODE_2,
  output OR_CONST,
  output OR_ADDRESS,
  output OR_ADDRESS_REGISTER,
  output OR_ADDRESS_REGISTER_PLUS_OFFSET,
  output STORE_ADDRESS,
  output STORE_ADDRESS_REGISTER,
  output STORE_ADDRESS_REGISTER_PLUS_OFFSET,
  output LOAD_ADDRESS_REGISTER_CONST,
  output LOAD_ADDRESS_REGISTER_ADDRESS,
  output NOT,
  output JUMP_ADDRESS,
  output JUMP_ZERO,
  output JUMP_NEGATIVE,
  output JUMP_ERROR,
  output JUMP_NOT_ERROR,
  output CLEAR_ERROR,
  output INPUT,
  output PRINT,
  output PRINT_ADDRESS,
  output HALT,
  output SET_OVF,
  output SET_DIV0,
  output SET_ADDR,
  output SET_INV,
  output SET_ILL,
  output SET_INPUT
);

  wire PC_RANGE_eq, PC_SOURCE_p1;
  wire [15:0] PC_INCREMENT_out;
  wire [15:12] PC_q;

  Register #(.width(16)) PC (.D(PC_INCREMENT_out), .clk(CLK), .Q({PC_q, PC_OUT[11:1], NOT}), .clr(RESET));  // open: en
  Comparator #(.width(16)) PC_RANGE (
    .a(PROGRAM_LIMIT), .b({PC_q, PC_OUT[11:1], NOT}), .eq(PC_RANGE_eq));  // open: gt, lt
  Adder #(.width(16)) PC_INCREMENT (
    .a({PC_q, PC_OUT[11:1], NOT}), .b({16{1'b1}}), .out(PC_INCREMENT_out));  // open: cin, cout
  ROM #(.addrWidth(12), .dataWidth(22)) INSTRUCTION_ROM (.addr({PC_OUT[11:1], NOT}), .data(OPCODE_2));
  Decoder #(.select(6)) ISA_DECODER (
    .out0(LOAD_ADDRESS), .out1(LOAD_ADDRESS_REGISTER), .out2(LOAD_ADDRESS_REGISTER_PLUS_OFFSET),
    .out3(ADD_CONST), .out4(ADD_ADDRESS_REGISTER), .out5(ADD_ADDRESS_REGISTER_PLUS_OFFSET), .out6(SUB_CONST),
    .out7(SUB_ADDRESS), .out8(SUB_ADDRESS_REGISTER), .out9(SUB_ADDRESS_REGISTER_PLUS_OFFSET),
    .out10(MUL_CONST), .out11(MUL_ADDRESS), .out12(MUL_ADDRESS_REGISTER),
    .out13(MUL_ADDRESS_REGISTER_PLUS_OFFSET), .out14(DIV_CONST), .out15(DIV_ADDRESS),
    .out16(DIV_ADDRESS_REGISTER), .out17(DIV_ADDRESS_REGISTER_PLUS_OFFSET), .out18(AND_CONST),
    .out19(AND_ADDRESS), .out20(AND_ADDRESS_REGISTER), .out21(AND_ADDRESS_REGISTER_PLUS_OFFSET),
    .out22(OR_CONST), .out23(OR_ADDRESS), .out24(OR_ADDRESS_REGISTER),
    .out25(OR_ADDRESS_REGISTER_PLUS_OFFSET), .out26(STORE_ADDRESS_REGISTER),
    .out27(STORE_ADDRESS_REGISTER_PLUS_OFFSET), .out28(LOAD_ADDRESS_REGISTER_CONST),
    .out29(LOAD_ADDRESS_REGISTER_ADDRESS), .out30(NOT), .out31(JUMP_ADDRESS), .out32(JUMP_ZERO),
    .out33(JUMP_NEGATIVE), .out34(JUMP_ERROR), .out35(JUMP_NOT_ERROR), .out36(CLEAR_ERROR), .out37(INPUT),
    .out38(PRINT_ADDRESS), .out39(SET_OVF), .out40(SET_DIV0), .out41(SET_INV), .out42(SET_ILL),
    .out43(SET_INPUT), .sel(OPCODE));  // open: out44, out45, out46, out47, out48, out49, out50, out51, out52, out53, out54, out55, out56, out57, out58, out59, out60, out61, out62, out63, en
  // Multiplexer #(.width(16)) PC_SOURCE: pin names not known; wires that end beside it: PC_SOURCE_p1
  // AND_Gate JNZ_TAKEN: pin names not known; wires that end beside it: DEC_JUMP_NOT_ZERO, NOT_ZERO, JUMP_NOT_ZERO
  or ERROR_HALT (AND_CONST, PC_RANGE_eq, DEC_HALT_ERROR);
  // Pins of 1 and 12 and 16 bits meet at {PC_OUT[15:1], NOT}

  assign HALT_ERROR = AND_CONST;
  assign PC_OUT[0] = NOT;

  // Notes on the sheet:
  //   PROGRAM_LIMIT: initial=0xfff
  //   AP 7 machine format v1: stable six-bit opcode allocation and encoder-generated ROM
  //   contents of INSTRUCTION_ROM (hex, n*v repeats v):
  //   3fffff 65 3 64 0 65 64 4
endmodule
