// Logisim project TinyCPU-FetchDecode1.circ as structural Verilog: 1 circuit, main circuit FetchDecode
module FetchDecode (
  input  CLK,
  input  RESET,
  input  ZERO,
  input  [11:0] PROGRAM_LIMIT,
  input  NEGATIVE,
  input  ERROR,
  output [11:0] PC_OUT,
  output [21:0] INSTRUCTION
);

  wire adder_1_p2;
  wire [11:0] PC_p1;

  // Register #(.width(12)) PC: pin names not known; wires that end beside it: PC_p1, CLK, RESET, PC_OUT
  // Adder #(.width(12)) adder_1: pin names not known; wires that end beside it: PC_OUT, adder_1_p2, adder_1_p2
  Multiplexer #(.width(12)) multiplexer_1 (.out(PC_p1));  // open: in0, in1, sel
  ROM #(.addrWidth(12), .dataWidth(22)) INSTRUCTION_ROM (.addr(PC_OUT));  // open: data
  // Comparator #(.width(12)) comparator_1: pin names not known; wires that end beside it: PC_OUT, PROGRAM_LIMIT, ERROR

  assign NEGATIVE = ERROR;
  assign ZERO = ERROR;

  // Notes on the sheet:
  //   AP 7 machine format v1: stable six-bit opcode allocation and encoder-generated ROM
  //   contents of INSTRUCTION_ROM (hex, n*v repeats v):
  //   ffff 1c0065 3 1c0064 2a0000 50065 1c0064 240004 2c0000
endmodule
