// Logisim project TinyCPU-FetchDecode2.circ as structural Verilog: 1 circuit, main circuit FetchDecode
module FetchDecode (
  input  [15:0] OPERAND_IN,
  input  DEC_LOAD_CONST,
  input  DEC_STORE_ADDRESS,
  input  DEC_ADD_ADDRESS,
  input  DEC_JUMP_NOT_ZERO,
  input  ZERO,
  input  DEC_PRINT,
  input  ERROR,
  input  DEC_HALT,
  input  DEC_SET_ADDR,
  input  DEC_HALT_ERROR,
  input  [11:0] PC_IN,
  output [15:0] OPERAND,
  output LOAD_CONST,
  output STORE_ADDRESS,
  output ADD_ADDRESS,
  output JUMP_NOT_ZERO,
  output PRINT,
  output HALT,
  output SET_ADDR,
  output HALT_ERROR,
  output [11:0] PC_OUT
);

  // AND_Gate JNZ_TAKEN has open pins: out=DEC_JUMP_NOT_ZERO
  // OR_Gate ERROR_HALT has open pins: out=DEC_HALT_ERROR

  assign ADD_ADDRESS = DEC_ADD_ADDRESS;
  assign ERROR = DEC_HALT_ERROR;
  assign HALT = DEC_HALT;
  assign HALT_ERROR = DEC_HALT_ERROR;
  assign JUMP_NOT_ZERO = DEC_JUMP_NOT_ZERO;
  assign LOAD_CONST = DEC_LOAD_CONST;
  assign OPERAND = OPERAND_IN;
  assign PC_OUT = PC_IN;
  assign PRINT = DEC_PRINT;
  assign SET_ADDR = DEC_SET_ADDR;
  assign STORE_ADDRESS = DEC_STORE_ADDRESS;
  assign ZERO = DEC_JUMP_NOT_ZERO;

  // Notes on the sheet:
  //   AP 7 machine format v1: stable six-bit opcode allocation and encoder-generated ROM
endmodule
