// Logisim project TinyCPU-FetchDecode3.circ as structural Verilog: 1 circuit, main circuit FetchDecode3
module FetchDecode3 (
  input  [5:0] OPCODE,
  output LOAD_ADDRESS,
  output LOAD_ADDRESS_REGISTER,
  output LOAD_ADDRESS_REGISTER_PLUS_OFFSET,
  output ADD_CONST,
  output ADD_ADDRESS_REGISTER,
  output ADD_ADDRESS_REGISTER_PLUS_OFFSET,
  output SUB_CONST,
  output SUB_ADDRESS,
  output SUB_ADDRESS_REGISTER,
  output SUB_ADDRESS_REGISTER_PLUS_OFFSET,
  output MUL_CONST,
  output MUL_ADDRESS,
  output MUL_ADDRESS_REGISTER,
  output MUL_ADDRESS_REGISTER_PLUS_OFFSET,
  output DIV_CONST,
  output DIV_ADDRESS,
  output DIV_ADDRESS_REGISTER,
  output DIV_ADDRESS_REGISTER_PLUS_OFFSET,
  output AND_CONST,
  output AND_ADDRESS,
  output AND_ADDRESS_REGISTER,
  output AND_ADDRESS_REGISTER_PLUS_OFFSET,
  output OR_CONST,
  output OR_ADDRESS,
  output OR_ADDRESS_REGISTER,
  output OR_ADDRESS_REGISTER_PLUS_OFFSET,
  output STORE_ADDRESS_REGISTER,
  output STORE_ADDRESS_REGISTER_PLUS_OFFSET,
  output LOAD_ADDRESS_REGISTER_CONST,
  output LOAD_ADDRESS_REGISTER_ADDRESS,
  output NOT,
  output JUMP_ADDRESS,
  output JUMP_ZERO,
  output JUMP_NEGATIVE,
  output JUMP_ERROR,
  output JUMP_NOT_ERROR,
  output CLEAR_ERROR,
  output INPUT,
  output PRINT_ADDRESS,
  output SET_OVF,
  output SET_DIV0,
  output SET_INV,
  output SET_ILL,
  output SET_INPUT
);

  Decoder #(.select(6)) decoder_1 (
    .out1(ADD_ADDRESS_REGISTER_PLUS_OFFSET), .out3(SUB_CONST), .out5(SUB_ADDRESS),
    .out7(SUB_ADDRESS_REGISTER), .out9(SUB_ADDRESS_REGISTER_PLUS_OFFSET), .out11(MUL_CONST),
    .out13(MUL_ADDRESS), .out15(MUL_ADDRESS_REGISTER), .out17(MUL_ADDRESS_REGISTER_PLUS_OFFSET),
    .out19(DIV_CONST), .out21(DIV_ADDRESS), .out23(DIV_ADDRESS_REGISTER),
    .out25(DIV_ADDRESS_REGISTER_PLUS_OFFSET), .out27(AND_CONST), .out29(AND_ADDRESS),
    .out31(AND_ADDRESS_REGISTER), .out33(AND_ADDRESS_REGISTER_PLUS_OFFSET), .out35(OR_CONST),
    .out37(OR_ADDRESS), .out39(OR_ADDRESS_REGISTER), .out41(OR_ADDRESS_REGISTER_PLUS_OFFSET),
    .out45(STORE_ADDRESS_REGISTER), .out47(STORE_ADDRESS_REGISTER_PLUS_OFFSET),
    .out49(LOAD_ADDRESS_REGISTER_CONST), .out51(LOAD_ADDRESS_REGISTER_ADDRESS), .out53(NOT),
    .out55(JUMP_ADDRESS), .out57(JUMP_ZERO), .out61(JUMP_NEGATIVE), .out63(JUMP_ERROR), .sel(OPCODE));  // open: out0, out2, out4, out6, out8, out10, out12, out14, out16, out18, out20, out22, out24, out26, out28, out30, out32, out34, out36, out38, out40, out42, out43, out44, out46, out48, out50, out52, out54, out56, out58, out59, out60, out62, en
endmodule
