// Logisim project TinyCPU-FetchDecodeControls.circ as structural Verilog: 1 circuit, main circuit FetchDecodeControls
module FetchDecodeControls (
  input  [5:0] OPCODE,
  output LOAD_CONST,
  output LOAD_ADDRESS,
  output LOAD_ADDRESS_REGISTER,
  output LOAD_ADDRESS_REGISTER_PLUS_OFFSET,
  output ADD_CONST,
  output ADD_ADDRESS,
  output ADD_ADDRESS_REGISTER,
  output ADD_ADDRESS_REGISTER_PLUS_OFFSET,
  output SUB_CONST,
  output SUB_ADDRESS,
  output SUB_ADDRESS_REGISTER,
  output SUB_ADDRESS_REGISTER_PLUS_OFFSET,
  output MUL_CONST,
  output MUL_ADDRESS,
  output MUL_ADDRESS_REGISTER,
  output MUL_ADDRESS_REGISTER_PLUS_OFFSET,
  output DIV_CONST,
  output DIV_ADDRESS,
  output DIV_ADDRESS_REGISTER,
  output DIV_ADDRESS_REGISTER_PLUS_OFFSET,
  output AND_CONST,
  output AND_ADDRESS,
  output AND_ADDRESS_REGISTER,
  output AND_ADDRESS_REGISTER_PLUS_OFFSET,
  output OR_CONST,
  output OR_ADDRESS,
  output OR_ADDRESS_REGISTER,
  output OR_ADDRESS_REGISTER_PLUS_OFFSET,
  output STORE_ADDRESS,
  output STORE_ADDRESS_REGISTER,
  output STORE_ADDRESS_REGISTER_PLUS_OFFSET,
  output LOAD_ADDRESS_REGISTER_CONST,
  output LOAD_ADDRESS_REGISTER_ADDRESS,
  output NOT,
  output JUMP_ADDRESS,
  output JUMP_ZERO,
  output JUMP_NEGATIVE,
  output JUMP_ERROR,
  output JUMP_NOT_ERROR,
  output CLEAR_ERROR,
  output INPUT,
  output PRINT,
  output PRINT_ADDRESS,
  output HALT,
  output HALT_ERROR,
  output SET_OVF,
  output SET_DIV0,
  output SET_ADDR,
  output SET_INV,
  output SET_ILL,
  output SET_INPUT
);

  Decoder #(.select(6)) DECODER_500_670 (
    .out0(LOAD_CONST), .out1(LOAD_ADDRESS), .out2(LOAD_ADDRESS_REGISTER),
    .out3(LOAD_ADDRESS_REGISTER_PLUS_OFFSET), .out4(ADD_CONST), .out5(ADD_ADDRESS),
    .out6(ADD_ADDRESS_REGISTER), .out7(ADD_ADDRESS_REGISTER_PLUS_OFFSET), .out8(SUB_CONST),
    .out9(SUB_ADDRESS), .out10(SUB_ADDRESS_REGISTER), .out11(SUB_ADDRESS_REGISTER_PLUS_OFFSET),
    .out12(MUL_CONST), .out13(MUL_ADDRESS), .out14(MUL_ADDRESS_REGISTER),
    .out15(MUL_ADDRESS_REGISTER_PLUS_OFFSET), .out16(DIV_CONST), .out17(DIV_ADDRESS),
    .out18(DIV_ADDRESS_REGISTER), .out19(DIV_ADDRESS_REGISTER_PLUS_OFFSET), .out20(AND_CONST),
    .out21(AND_ADDRESS), .out22(AND_ADDRESS_REGISTER), .out23(AND_ADDRESS_REGISTER_PLUS_OFFSET),
    .out24(OR_CONST), .out25(OR_ADDRESS), .out26(OR_ADDRESS_REGISTER),
    .out27(OR_ADDRESS_REGISTER_PLUS_OFFSET), .out28(STORE_ADDRESS), .out29(STORE_ADDRESS_REGISTER),
    .out30(STORE_ADDRESS_REGISTER_PLUS_OFFSET), .out31(LOAD_ADDRESS_REGISTER_CONST),
    .out32(LOAD_ADDRESS_REGISTER_ADDRESS), .out33(NOT), .out34(JUMP_ADDRESS), .out35(JUMP_ZERO),
    .out36(JUMP_NEGATIVE), .out37(JUMP_ERROR), .out38(JUMP_NOT_ERROR), .out39(CLEAR_ERROR), .out40(INPUT),
    .out41(PRINT), .out42(PRINT_ADDRESS), .out43(HALT), .out44(HALT_ERROR), .out45(SET_OVF),
    .out46(SET_DIV0), .out47(SET_ADDR), .out48(SET_INV), .out49(SET_ILL), .out50(SET_INPUT), .sel(OPCODE));  // open: out51, out52, out53, out54, out55, out56, out57, out58, out59, out60, out61, out62, out63, en
endmodule
