// Logisim project TinyCPU-IntegrationReset.circ as structural Verilog: 1 circuit, main circuit IntegrationReset
module IntegrationReset (
  input  RESET,
  output FETCH_RESET
);


  assign FETCH_RESET = RESET;
endmodule
