// Logisim project TinyCPU-Memory.circ as structural Verilog: 1 circuit, main circuit Memory
module Memory (
  input  [11:0] ADDRESS,
  input  [15:0] DATA_IN,
  input  VALID_IN,
  input  WRITE_ENABLE,
  input  CLK,
  output [15:0] DATA_OUT,
  output VALID_OUT
);

  wire DATA_RAM_p2, DATA_RAM_p3, DATA_RAM_p10;

  // RAM #(.addrWidth(12), .dataWidth(16)) DATA_RAM: pin names not known; wires that end beside it: DATA_IN, DATA_RAM_p2, DATA_RAM_p3, ADDRESS, VALID_IN, DATA_RAM_p2, DATA_RAM_p3, DATA_OUT, VALID_OUT, DATA_RAM_p10
  // RAM #(.addrWidth(12), .dataWidth(1)) VALID_RAM: pin names not known; wires that end beside it: VALID_IN, DATA_RAM_p2, DATA_RAM_p3, VALID_OUT, DATA_RAM_p10

  // Notes on the sheet:
  //   4096-word value/valid memory with shared address, write-enable, and clock
endmodule
