// Logisim project TinyCPU-NotCircuit.circ as structural Verilog: 1 circuit, main circuit NotCircuit
module NotCircuit (
  input  [15:0] ACC_VALUE,
  input  ACC_VALID,
  input  NOT_SELECT,
  output [15:0] RESULT,
  output OVERFLOW,
  output NOT_VALID,
  output NOT_SELECTED
);

  wire [15:0] NOT_VALUE_out;

  assign NOT_VALUE_out = ~ACC_VALUE;  // NOT_Gate NOT_VALUE, 16 bits wide
  Multiplexer #(.width(16)) ACTIVE_NOT_RESULT (.in0(16'h1), .in1(NOT_VALUE_out), .out(RESULT), .sel(NOT_SELECT));
  and ACTIVE_NOT_VALID (NOT_VALID, ACC_VALID, NOT_SELECT);

  assign NOT_SELECTED = NOT_SELECT;
  assign OVERFLOW = 1'b1;
endmodule
