// Logisim project TinyCPU-SubCircuit.circ as structural Verilog: 1 circuit, main circuit SubCircuit
module SubCircuit (
  input  [15:0] LEFT,
  input  [15:0] RIGHT,
  input  SUB_SELECT,
  input  INPUT_VALID,
  output [15:0] RESULT,
  output SUB_SELECTED,
  output OVERFLOW,
  output SUB_VALID
);

  wire NO_OVERFLOW_out, OPERAND_SIGN_DIFFERENT_out, RESULT_SIGN_CHANGED_out;

  Subtractor #(.width(16)) SUBTRACTOR_360_140 (.a(LEFT), .b(RIGHT), .out(RESULT));  // open: bin, bout
  xor OPERAND_SIGN_DIFFERENT (OPERAND_SIGN_DIFFERENT_out, LEFT[15], RIGHT[15]);
  xor RESULT_SIGN_CHANGED (RESULT_SIGN_CHANGED_out, RESULT[15], OPERAND_SIGN_DIFFERENT_out);
  and SIGN_OVERFLOW (OVERFLOW, RESULT_SIGN_CHANGED_out, OPERAND_SIGN_DIFFERENT_out);
  not NO_OVERFLOW (NO_OVERFLOW_out, OVERFLOW);
  and RANGE_VALID (SUB_VALID, NO_OVERFLOW_out, INPUT_VALID);

  assign SUB_SELECTED = SUB_SELECT;

  // Notes on the sheet:
  //   signed SUB: overflow = (left_sign XOR right_sign) AND (left_sign XOR result_sign)
endmodule
